// Logisim project Digital Design Assignment Logisim Implementation.circ as structural Verilog: 11 circuits, main circuit main
module main (
  input  Operation,
  output [3:0] Hundreds,
  output [3:0] Tens,
  output [3:0] Ones,
  output Operation_to_perform
);

  wire Decrease_out, Increase_out, keep_operation_constant_1_change, or_1_out, Piston_out,
       pull_in_and_push_out_pulse_generator_1__0__1_transition,
       pull_in_and_push_out_pulse_generator_1__1__0_transition, Reset_out;
  wire [3:0] display_2_hundreds, display_2_ones, display_2_tens;
  wire [7:0] counting_and_updating_1_current_value, counting_and_updating_1_set_new;

  Button Increase (.out(Increase_out));
  Button Decrease (.out(Decrease_out));
  Button Reset (.out(Reset_out));
  Button Piston (.out(Piston_out));
  or or_1 (or_1_out, Reset_out, pull_in_and_push_out_pulse_generator_1__1__0_transition);
  Keep_operation_constant keep_operation_constant_1 (
    .Operation(Operation), .Set_Value(counting_and_updating_1_set_new),
    .Real_Operation(Operation_to_perform), .Change(keep_operation_constant_1_change));
  pull_in_and_push_out_pulse_generator pull_in_and_push_out_pulse_generator_1 (
    .Piston(Piston_out), ._0__1_Transition(pull_in_and_push_out_pulse_generator_1__0__1_transition),
    ._1__0_Transition(pull_in_and_push_out_pulse_generator_1__1__0_transition));
  counting_and_updating counting_and_updating_1 (
    .Operation_to_perform(Operation_to_perform), .Piston(Piston_out), .Increase(Increase_out),
    .Decrease(Decrease_out), .Reset(or_1_out),
    ._0__1_transition(pull_in_and_push_out_pulse_generator_1__0__1_transition),
    .Current_value(counting_and_updating_1_current_value), .Set_New(counting_and_updating_1_set_new));
  display display_1 (.Input(counting_and_updating_1_set_new), .Tens(Tens), .Hundreds(Hundreds), .Ones(Ones));
  Hex_Digit_Display hex_digit_display_1 (.value(display_2_hundreds));  // open: dp
  display display_2 (
    .Input(counting_and_updating_1_current_value), .Tens(display_2_tens), .Hundreds(display_2_hundreds),
    .Ones(display_2_ones));
  Hex_Digit_Display hex_digit_display_2 (.value(display_2_ones));  // open: dp
  Hex_Digit_Display hex_digit_display_3 (.value(display_2_tens));  // open: dp
  Hex_Digit_Display hex_digit_display_4 (.value(Hundreds));  // open: dp
  Hex_Digit_Display hex_digit_display_5 (.value(Tens));  // open: dp
  Hex_Digit_Display hex_digit_display_6 (.value(Ones));  // open: dp
  LED Change_in_operation_detected (.in(keep_operation_constant_1_change));

  // Notes on the sheet:
  //   Operation as 0 indicates pull in and 1 indicates push out
  //   Current value
  //   Set value
  //   To the actuator giving number in BCD
endmodule

module counting_and_updating (
  input  Operation_to_perform,
  input  Piston,
  input  Increase,
  input  Decrease,
  input  Reset,
  input  _0__1_transition,
  output [7:0] Current_value,
  output [7:0] Set_New
);

  wire and_1_out, and_2_out, and_5_out, and_6_out, and_7_out, and_8_out, and_9_out, and_10_out,
       compare_with_0_and_20_1_with_0, compare_with_0_and_20_1_with_20,
       current_set_is_between_0_and_20_1_with_0, current_set_is_between_0_and_20_1_with_20,
       multiplexer_1_out, not_1_out, xor_1_out, xor_2_out, xor_3_out, xor_4_out;
  wire [7:0] and_4_out, current_set_is_between_0_and_20_1_sum, n8_bit_adder_1_out_4;

  not not_1 (not_1_out, Piston);
  and and_1 (and_1_out, not_1_out, Increase);
  and and_2 (and_2_out, not_1_out, Decrease);
  xor xor_1 (xor_1_out, and_1_out, and_2_out);
  _8_bit_register SETTER (.Input(n8_bit_adder_1_out_4), .Select_Line(xor_1_out), .Reset(Reset), .out_4(Set_New));
  and and_3 (and_4_out[7], and_2_out, and_4_out[0]);
  _8_bit_register STORE (
    .Input(current_set_is_between_0_and_20_1_sum), .Select_Line(_0__1_transition), .out_4(Current_value));  // open: Reset
  _8_bit_adder u_8_bit_adder_1 (
    .Num1(Set_New), .Num2({{7{and_4_out[7]}}, and_4_out[0]}), .out_4(n8_bit_adder_1_out_4));  // open: Cin
  Multiplexer multiplexer_1 (
    .in0(xor_2_out), .in1(xor_4_out), .out(multiplexer_1_out), .sel(Operation_to_perform));  // open: en
  and and_4 (and_4_out[0], multiplexer_1_out, xor_3_out);
  Current______set_is_between_0_and_20 current_set_is_between_0_and_20_1 (
    .operation(Operation_to_perform), .Current_value(Current_value), .Set_value(Set_New),
    .with_0(current_set_is_between_0_and_20_1_with_0), .with_20(current_set_is_between_0_and_20_1_with_20),
    .Sum(current_set_is_between_0_and_20_1_sum));
  Compare_with_0_and_20 compare_with_0_and_20_1 (
    .Input(Set_New), .with_0(compare_with_0_and_20_1_with_0), .with_20(compare_with_0_and_20_1_with_20));
  and and_5 (and_5_out, and_1_out, current_set_is_between_0_and_20_1_with_20);
  and and_6 (and_6_out, current_set_is_between_0_and_20_1_with_0, and_2_out);
  xor xor_2 (xor_2_out, and_5_out, and_6_out);
  and and_7 (and_7_out, compare_with_0_and_20_1_with_0, and_2_out);
  and and_8 (and_8_out, and_1_out, compare_with_0_and_20_1_with_20);
  xor xor_3 (xor_3_out, and_8_out, and_7_out);
  and and_9 (and_9_out, and_1_out, current_set_is_between_0_and_20_1_with_0);
  and and_10 (and_10_out, and_2_out, current_set_is_between_0_and_20_1_with_20);
  xor xor_4 (xor_4_out, and_9_out, and_10_out);

  // Notes on the sheet:
  //   When both are 
  //   are pressed at
  //   the same time 
  //   no change in set
  //   Reseting at 1->0 transition hence updating at 0->1 transition
  //   Ensuring that the value
  //   doesn't change when piston
  //   is pushed
  //   Adding 1 or its 2's complement
  //   based on the operation
  //   Ensuring the value of current(+/-)set
  //   and set are between 0 and 20
endmodule

module Compare_with_0_and_20 (
  input  [7:0] Input,
  output with_0,
  output with_20
);

  Comparator #(.mode("unsigned")) comparator_1 (.a(Input), .b({8{1'b0}}), .gt(with_0));  // open: eq, lt
  Comparator #(.mode("unsigned")) comparator_2 (.a(Input), .b(8'h14), .lt(with_20));  // open: gt, eq
endmodule

module pull_in_and_push_out_pulse_generator (
  input  Piston,
  output _0__1_Transition,
  output _1__0_Transition
);

  wire CLK_out, d_ff_1_q, d_ff_2_q, not_1_out;

  Clock CLK (.out(CLK_out));
  not not_1 (not_1_out, Piston);
  J_K_Flip_Flop #(.trigger("falling")) j_k_ff_1 (
    .J(1'b1), .clk(not_1_out), .K(1'b1), .Q(_0__1_Transition), .reset(d_ff_1_q));  // open: Qn, preset, en
  D_Flip_Flop d_ff_1 (.clk(CLK_out), .D(_0__1_Transition), .Q(d_ff_1_q));  // open: Qn, preset, en, reset
  J_K_Flip_Flop #(.trigger("falling")) j_k_ff_2 (
    .J(1'b1), .clk(Piston), .K(1'b1), .Q(_1__0_Transition), .reset(d_ff_2_q));  // open: Qn, preset, en
  D_Flip_Flop d_ff_2 (.clk(CLK_out), .D(_1__0_Transition), .Q(d_ff_2_q));  // open: Qn, preset, en, reset
endmodule

module Keep_operation_constant (
  input  Operation,
  input  [7:0] Set_Value,
  output Real_Operation,
  output Change
);

  wire clock_1_out, comparator_1_eq, multiplexer_1_out;

  Clock clock_1 (.out(clock_1_out));
  Comparator #(.mode("unsigned")) comparator_1 (.a(Set_Value), .b({8{1'b0}}), .eq(comparator_1_eq));  // open: gt, lt
  Multiplexer multiplexer_1 (
    .in0(Real_Operation), .in1(Operation), .out(multiplexer_1_out), .sel(comparator_1_eq));  // open: en
  D_Flip_Flop d_ff_1 (.clk(clock_1_out), .D(multiplexer_1_out), .Q(Real_Operation));  // open: Qn, preset, en, reset
  xor xor_1 (Change, Real_Operation, Operation);

  // Notes on the sheet:
  //   This circuit ensures that the operation doesnt change after a value has been set 
endmodule

module display (
  input  [7:0] Input,
  output [3:0] Tens,
  output [3:0] Hundreds,
  output [3:0] Ones
);

  _6_bit_Binary_To_BCD_converter u_6_bit_binary_to_bcd_converter_1 (
    .A(Input[4]), .B(Input[3]), .C(Input[2]), .D(Input[1]), .E(Input[0]), .F(Input[5]), .A3(Tens[3]),
    .A2(Tens[2]), .A1(Tens[1]), .A0(Tens[0]), .B1(Hundreds[1]), .B0(Hundreds[0]));

  assign Hundreds[3:2] = 2'b00;
  assign Ones = 4'b0000;

  // Notes on the sheet:
  //   The 5th,6h,7th bits are insignificant as the circuit converts a binary number to a number between 0 to 20.
endmodule

module Current______set_is_between_0_and_20 (
  input  operation,
  input  [7:0] Current_value,
  input  [7:0] Set_value,
  output with_0,
  output with_20,
  output [7:0] Sum
);

  wire [7:0] conditionally_negate_1_out_3;

  conditionally_negate conditionally_negate_1 (
    .operation(operation), .Value_to_change(Set_value), .out_3(conditionally_negate_1_out_3));
  _8_bit_adder u_8_bit_adder_1 (
    .Cin(operation), .Num1(Current_value), .Num2(conditionally_negate_1_out_3), .out_4(Sum));
  Compare_with_0_and_20 compare_with_0_and_20_1 (.Input(Sum), .with_0(with_0), .with_20(with_20));

  // Notes on the sheet:
  //   This circuit ensures that the sum of current value and set value is between 0 and 20
endmodule

module conditionally_negate (
  input  operation,
  input  [7:0] Value_to_change,
  output [7:0] out_3
);

  xor xor_1 (out_3[0], operation, Value_to_change[0]);
  xor xor_2 (out_3[1], operation, Value_to_change[1]);
  xor xor_3 (out_3[2], operation, Value_to_change[2]);
  xor xor_4 (out_3[3], operation, Value_to_change[3]);
  xor xor_5 (out_3[4], operation, Value_to_change[4]);

  assign out_3[7:5] = {3{operation}};
endmodule

module _8_bit_adder (
  input  Cin,
  input  [7:0] Num1,
  input  [7:0] Num2,
  output [7:0] out_4
);

  wire adder_1_cout;

  Adder #(.width(4)) adder_1 (.a(Num1[3:0]), .b(Num2[3:0]), .out(out_4[3:0]), .cin(Cin), .cout(adder_1_cout));
  Adder #(.width(4)) adder_2 (.a(Num1[7:4]), .b(Num2[7:4]), .out(out_4[7:4]), .cin(adder_1_cout));  // open: cout
endmodule

module _8_bit_register (
  input  [7:0] Input,
  input  Select_Line,
  input  Reset,
  output [7:0] out_4
);

  wire CLK_out, multiplexer_1_out, multiplexer_2_out, multiplexer_3_out, multiplexer_4_out,
       multiplexer_5_out, multiplexer_6_out, multiplexer_7_out, multiplexer_8_out, undriven;

  Clock CLK (.out(CLK_out));
  Multiplexer multiplexer_1 (.in0(out_4[0]), .in1(Input[0]), .out(multiplexer_1_out), .sel(Select_Line));  // open: en
  Multiplexer multiplexer_2 (.in0(out_4[1]), .in1(Input[1]), .out(multiplexer_2_out), .sel(Select_Line));  // open: en
  Multiplexer multiplexer_3 (.in0(out_4[2]), .in1(Input[2]), .out(multiplexer_3_out), .sel(Select_Line));  // open: en
  Multiplexer multiplexer_4 (.in0(out_4[3]), .in1(Input[3]), .out(multiplexer_4_out), .sel(Select_Line), .en(undriven));
  Multiplexer multiplexer_5 (.in0(out_4[4]), .in1(Input[4]), .out(multiplexer_5_out), .sel(Select_Line));  // open: en
  Multiplexer multiplexer_6 (.in0(out_4[5]), .in1(Input[5]), .out(multiplexer_6_out), .sel(Select_Line));  // open: en
  Multiplexer multiplexer_7 (.in0(out_4[6]), .in1(Input[6]), .out(multiplexer_7_out), .sel(Select_Line));  // open: en
  Multiplexer multiplexer_8 (.in0(out_4[7]), .in1(Input[7]), .out(multiplexer_8_out), .sel(Select_Line));  // open: en
  D_Flip_Flop d_ff_1 (.clk(CLK_out), .D(multiplexer_1_out), .Q(out_4[0]), .reset(Reset));  // open: Qn, preset, en
  D_Flip_Flop d_ff_2 (.clk(CLK_out), .D(multiplexer_2_out), .Q(out_4[1]), .reset(Reset));  // open: Qn, preset, en
  D_Flip_Flop d_ff_3 (.clk(CLK_out), .D(multiplexer_3_out), .Q(out_4[2]), .reset(Reset));  // open: Qn, preset, en
  D_Flip_Flop d_ff_4 (.clk(CLK_out), .D(multiplexer_4_out), .Q(out_4[3]), .reset(Reset));  // open: Qn, preset, en
  D_Flip_Flop d_ff_5 (.clk(CLK_out), .D(multiplexer_5_out), .Q(out_4[4]), .reset(Reset));  // open: Qn, preset, en
  D_Flip_Flop d_ff_6 (.clk(CLK_out), .D(multiplexer_6_out), .Q(out_4[5]), .reset(Reset));  // open: Qn, preset, en
  D_Flip_Flop d_ff_7 (.clk(CLK_out), .D(multiplexer_7_out), .Q(out_4[6]), .reset(Reset));  // open: Qn, preset, en
  D_Flip_Flop d_ff_8 (.clk(CLK_out), .D(multiplexer_8_out), .Q(out_4[7]), .reset(Reset));  // open: Qn, preset, en
endmodule

module _6_bit_Binary_To_BCD_converter (
  input  A,
  input  B,
  input  C,
  input  D,
  input  E,
  input  F,
  output A3,
  output A2,
  output A1,
  output A0,
  output B1,
  output B0
);

  wire and_2_out, and_3_out, and_4_out, and_5_out, and_6_out, and_7_out, and_8_out, and_9_out, and_10_out,
       and_11_out, and_12_out, and_13_out, and_14_out, and_15_out, and_16_out, and_17_out, and_18_out,
       and_19_out, and_20_out, and_21_out, and_22_out, and_23_out, and_24_out, and_25_out, and_26_out,
       and_27_out, not_1_out, not_2_out, not_3_out, not_4_out, not_5_out, not_6_out, not_7_out, not_8_out,
       not_9_out, not_10_out, not_11_out, not_12_out, not_13_out, not_14_out, not_15_out, not_16_out,
       or_1_out, or_2_out, or_3_out, or_4_out, or_5_out, or_6_out, or_7_out;

  not not_1 (not_1_out, C);
  not not_2 (not_2_out, A);
  not not_3 (not_3_out, B);
  not not_4 (not_4_out, B);
  not not_5 (not_5_out, C);
  not not_6 (not_6_out, A);
  not not_7 (not_7_out, B);
  not not_8 (not_8_out, C);
  not not_9 (not_9_out, D);
  and and_1 (B1, A, C);
  not not_10 (not_10_out, D);
  and and_2 (and_2_out, B, not_1_out);
  not not_11 (not_11_out, D);
  not not_12 (not_12_out, B);
  and and_3 (and_3_out, not_2_out, not_3_out);
  and and_4 (and_4_out, not_4_out, C);
  and and_5 (and_5_out, A, not_5_out);
  not not_13 (not_13_out, D);
  and and_6 (and_6_out, not_6_out, not_7_out);
  and and_7 (and_7_out, B, C);
  not not_14 (not_14_out, D);
  and and_8 (and_8_out, A, not_8_out);
  not not_15 (not_15_out, D);
  and and_9 (and_9_out, A, not_9_out);
  not not_16 (not_16_out, C);
  and and_10 (and_10_out, A, not_10_out);
  and and_11 (and_11_out, and_2_out, not_11_out);
  and and_12 (and_12_out, A, D);
  and and_13 (and_13_out, A, not_12_out);
  and and_14 (and_14_out, C, E);
  and and_15 (and_15_out, and_3_out, C);
  and and_16 (and_16_out, and_4_out, E);
  and and_17 (and_17_out, C, D);
  and and_18 (and_18_out, and_5_out, not_13_out);
  and and_19 (and_19_out, and_6_out, D);
  and and_20 (and_20_out, and_7_out, not_14_out);
  and and_21 (and_21_out, and_8_out, not_15_out);
  and and_22 (and_22_out, and_9_out, E);
  and and_23 (and_23_out, B, D);
  and and_24 (and_24_out, B, C);
  and and_25 (and_25_out, A, not_16_out);
  and and_26 (and_26_out, and_10_out, E);
  or or_1 (or_1_out, and_11_out, and_12_out);
  and and_27 (and_27_out, and_13_out, and_14_out);
  or or_2 (or_2_out, and_15_out, and_16_out);
  or or_3 (or_3_out, and_17_out, and_18_out);
  or or_4 (or_4_out, and_19_out, and_20_out);
  or or_5 (or_5_out, and_21_out, and_22_out);
  or or_6 (or_6_out, and_23_out, and_24_out);
  or or_7 (or_7_out, and_25_out, and_26_out);
  or or_8 (A3, or_1_out, and_27_out);
  or or_9 (A2, or_2_out, or_3_out);
  or or_10 (A1, or_4_out, or_5_out);
  or or_11 (B0, or_6_out, or_7_out);

  assign A0 = E;
endmodule
